# Fritzing sketch circuito (saved by Fritzing 0.9.3b)
breadboards: 1

parts:
  R1 = Photocell (LDR) [package=THT]
  U1 = ESP8266 NodeMCU LoLin module
  R2 = Resistor [tolerance=±5% resistance=220 package=THT]
  LED1 = LED - 5mm [color="Green (555nm)" package="5 mm [THT]"]
  LED2 = LED - 5mm [color="Red (635nm)" package="5 mm [THT]"]
  R3 = Resistor [tolerance=±5% resistance=220 package=THT]
  R4 = Resistor [tolerance=±5% resistance=220 package=THT]

nets:
  N1: R1.pin_0, U1.A0, R2.Pin_1
  N2: R1.pin_1, U1.Vin
  N3: U1.D3, R4.Pin_0
  N4: U1.D4, R3.Pin_0
  N5: U1.GND, U1.RST, R2.Pin_0, LED1.cathode, LED2.cathode
  N6: LED1.anode, R4.Pin_1
  N7: LED2.anode, R3.Pin_1

custom parts:
  ESP8266 NodeMCU LoLin module: ESP8266 based NodeMCU
